// Digital circuit MUX.dig as structural Verilog
module MUX (
  input  A,
  input  D,
  input  _5V,
  output Y
);

  wire and_1_out, and_2_out, not_1_out, not_2_out;

  not not_1 (not_1_out, A);
  not not_2 (not_2_out, D);
  and and_1 (and_1_out, _5V, _5V, not_1_out, D);
  and and_2 (and_2_out, A, not_2_out, _5V, _5V);
  or or_1 (Y, and_1_out, and_2_out);
endmodule
